# Fritzing sketch KTVXL (saved by Fritzing 0.9.3b)

parts:
  U1 = LIPO-110mAh [package=lipo-110]
  OLED_I2C1 = OLED 128x64 I2C Monochrome Display
  M1 = TP4056 Module [part_number=HW-107]
  ESP32_-_Back1 = ESP32 - CAM
  U2 = SWITCH_SPDT [package=kps-1290]

nets:
  N1: U1.+, U2.P
  N2: U1.-, ESP32_-_Back1.GND#12
  N3: OLED_I2C1.SDA, ESP32_-_Back1.GPIO15
  N4: OLED_I2C1.SCK, ESP32_-_Back1.GPIO14
  VDD: OLED_I2C1.VDD, ESP32_-_Back1.5V
  N5: OLED_I2C1.GND, ESP32_-_Back1.GND#7
  N6: M1.BAT+, U2.O
  N7: ESP32_-_Back1.3.3V, U2.S

notes:
  Mạch sạc TP4056
  Pin 18650-1200mAh 3.7V
  ESP32-CAM
  OLED 128x64

custom parts:
  TP4056 Module: TP4056 Lithium Battery Charge Management Module Links: TP4056 website
  ESP32 - CAM: The ESP32-CAM has a very competitive small-size camera module that can operate independently as a minimum system with a footprint of only 27*40.5*4.5mm and a deep sleep current of up to 6mA.
